// Logisim project lista4_2.circ as structural Verilog: 1 circuit, main circuit main
module main (
  input  T,
  input  PT,
  input  S,
  input  PS,
  output MD,
  output MS
);

  and and_1 (MD, T, PT);
  and and_2 (MS, S, PS);
endmodule
