// Logisim project lista4_3.circ as structural Verilog: 1 circuit, main circuit main
module main (
  input  H,
  input  m0,
  input  SF,
  input  P,
  output out_5
);

  wire and_1_out, and_2_out;

  and and_1 (and_1_out, H, m0);
  and and_2 (and_2_out, SF, P, m0);
  or or_1 (out_5, and_1_out, and_2_out);
endmodule
