// Logisim project lista4_4.circ as structural Verilog: 1 circuit, main circuit main
module main (
);


  // Notes on the sheet:
  //   i0
  //   i1
  //   A
  //   i0 e i1 = entradas digitais
  //   A = variavel de entrada seletora
  //   S = saida
  //   convenção: A=0 =>  i0,  A=1 => i1
  //   Circuito 
  //   lógico
  //   S
endmodule
