// Logisim project lista4_8.circ as structural Verilog: 1 circuit, main circuit main
module main (
  input  B,
  input  A,
  input  C,
  output Ev,
  output Bo
);

  wire not_2_out;

  not not_1 (Ev, A);
  not not_2 (not_2_out, C);
  and and_1 (Bo, B, not_2_out);

  // Notes on the sheet:
  //   eletrovalvula
  //   bomba
endmodule
