// Logisim project circuito_29.circ as structural Verilog: 1 circuit, main circuit main
module main (
  input  in_1,
  input  in_2,
  input  in_3,
  output out_4
);

  wire and_1_out, nand_1_out, nand_2_out, nand_3_out, nor_1_out, not_1_out, not_2_out;

  not not_1 (not_1_out, in_1);
  not not_2 (not_2_out, in_2);
  nand nand_1 (nand_1_out, in_2, in_3);
  nand nand_2 (nand_2_out, not_1_out, not_2_out, in_3);
  nand nand_3 (nand_3_out, in_1, in_3);
  and and_1 (and_1_out, nand_1_out, nand_2_out);
  nor nor_1 (nor_1_out, nand_3_out, in_2);
  or or_1 (out_4, in_1, and_1_out, nor_1_out);
endmodule
