// Logisim project circuito_3.circ as structural Verilog: 1 circuit, main circuit main
module main (
  input  A,
  input  B,
  input  C,
  output out_4
);

  wire and_1_out, and_2_out, nor_1_out, not_1_out, not_2_out, not_3_out, not_4_out, not_5_out, or_1_out;

  not not_1 (not_1_out, A);
  not not_2 (not_2_out, A);
  not not_3 (not_3_out, B);
  not not_4 (not_4_out, B);
  nor nor_1 (nor_1_out, A, C);
  and and_1 (and_1_out, not_2_out, not_3_out, C);
  and and_2 (and_2_out, not_4_out, nor_1_out);
  or or_1 (or_1_out, and_1_out, and_2_out);
  not not_5 (not_5_out, or_1_out);
  and and_3 (out_4, not_1_out, not_5_out);
endmodule
