// Logisim project circuito_2.circ as structural Verilog: 1 circuit, main circuit main
module main (
  input  A,
  input  B,
  input  C,
  input  D,
  output out_5
);

  wire and_1_out, nand_1_out, not_1_out, not_2_out, not_3_out, not_4_out, not_5_out, or_1_out, or_2_out,
       xnor_1_out;

  not not_1 (not_1_out, B);
  not not_2 (not_2_out, A);
  not not_3 (not_3_out, D);
  and and_1 (and_1_out, not_1_out, D);
  not not_4 (not_4_out, D);
  xnor xnor_1 (xnor_1_out, B, C);
  or or_1 (or_1_out, and_1_out, not_4_out);
  or or_2 (or_2_out, not_2_out, xnor_1_out, not_3_out);
  not not_5 (not_5_out, D);
  not nand_1 (nand_1_out, or_1_out);  // NAND_Gate
  or or_3 (out_5, or_2_out, not_5_out, nand_1_out);
endmodule
