// Logisim project lista4_1.circ as structural Verilog: 1 circuit, main circuit main
module main (
  input  m1,
  input  m2,
  input  m3,
  input  m4,
  output s1,
  output s2,
  output s3,
  output s4
);

  wire and_1_out, and_2_out, and_3_out, and_4_out, and_5_out, not_1_out, not_2_out, not_3_out, not_4_out;

  not not_1 (not_1_out, m1);
  not not_2 (not_2_out, m2);
  not not_3 (not_3_out, m3);
  not not_4 (not_4_out, m4);
  and and_1 (and_1_out, not_1_out, m3);
  and and_2 (and_2_out, not_2_out, m3);
  and and_3 (and_3_out, not_1_out, not_2_out, m4);
  and and_4 (and_4_out, not_1_out, not_3_out, m4);
  and and_5 (and_5_out, not_2_out, not_3_out, m4);
  or or_1 (s3, and_1_out, and_2_out);
  or or_2 (s4, and_3_out, and_4_out, and_5_out);

  assign s1 = m1;
  assign s2 = m2;
endmodule
