// Logisim project lista4_11.circ as structural Verilog: 1 circuit, main circuit main
module main (
  input  Far,
  input  Por,
  input  Ign,
  output S
);

  wire and_1_out, and_2_out, not_1_out;

  not not_1 (not_1_out, Ign);
  and and_1 (and_1_out, Far, not_1_out);
  or or_1 (S, and_1_out, and_2_out);
  and and_2 (and_2_out, Por, Ign);
endmodule
