// Logisim project lista4_6.circ as structural Verilog: 1 circuit, main circuit main
module main (
  input  A,
  input  B,
  input  C,
  output M1
);

  wire and_1_out, and_2_out, not_1_out, xnor_1_out, xor_1_out;

  not not_1 (not_1_out, C);
  xor xor_1 (xor_1_out, A, B);
  and and_1 (and_1_out, xor_1_out, C);
  and and_2 (and_2_out, not_1_out, xnor_1_out);
  xnor xnor_1 (xnor_1_out, A, B);
  or or_1 (M1, and_1_out, and_2_out);

  // Notes on the sheet:
  //   COM 5 ENTRADAS É MUITO TRABALHOSO.
endmodule
