// Logisim project lista4_7.circ as structural Verilog: 1 circuit, main circuit main
module main (
  input  A,
  input  B,
  input  C,
  input  D,
  output MS
);

  wire and_1_out, and_2_out;

  and and_1 (and_1_out, A, B);
  or or_1 (MS, and_1_out, and_2_out);
  and and_2 (and_2_out, B, C, D);
endmodule
