// Logisim project lista4_9.circ as structural Verilog: 1 circuit, main circuit main
module main (
  input  a,
  input  b,
  input  c
);

  wire and_1_out, and_2_out, or_1_out;

  and and_1 (and_1_out, a, c);
  and and_2 (and_2_out, b, c);
  or or_1 (or_1_out, and_1_out, and_2_out);
endmodule
