// Logisim project circuito_1.circ as structural Verilog: 1 circuit, main circuit main
module main (
  input  A,
  input  B,
  input  C,
  input  D,
  output out_5
);

  wire nand_1_out, nor_1_out, not_1_out, not_2_out, not_3_out, not_4_out, or_1_out;

  not not_1 (not_1_out, D);
  not not_2 (not_2_out, B);
  or or_1 (or_1_out, not_1_out, B, A);
  nor nor_1 (nor_1_out, A, not_2_out, C);
  not not_3 (not_3_out, A);
  not not_4 (not_4_out, C);
  nand nand_1 (nand_1_out, or_1_out, nor_1_out);
  and and_1 (out_5, nand_1_out, not_3_out, B, not_4_out);
endmodule
