// Logisim project circuito_26.circ as structural Verilog: 1 circuit, main circuit main
module main (
  input  in_1,
  input  in_2,
  input  in_3,
  output out_4
);

  wire nand_1_out, not_1_out;

  not not_1 (not_1_out, in_3);
  nand nand_1 (nand_1_out, in_1, in_2);
  or or_1 (out_4, nand_1_out, not_1_out);
endmodule
