// Logisim project circuito_5.circ as structural Verilog: 1 circuit, main circuit main
module main (
  input  A,
  input  B,
  input  C,
  input  D,
  output out_5
);

  wire and_1_out, and_2_out, and_3_out, and_4_out, and_5_out, and_6_out, nor_1_out, nor_2_out, nor_3_out,
       not_1_out, not_2_out, not_3_out, not_4_out, not_5_out, not_6_out, not_7_out, not_8_out, or_1_out,
       xor_1_out;

  not not_1 (not_1_out, A);
  not not_2 (not_2_out, B);
  not not_3 (not_3_out, B);
  xor xor_1 (xor_1_out, B, C);
  not not_4 (not_4_out, A);
  not not_5 (not_5_out, B);
  not not_6 (not_6_out, D);
  not not_7 (not_7_out, C);
  not not_8 (not_8_out, B);
  or or_1 (or_1_out, not_1_out, not_2_out);
  and and_1 (and_1_out, not_4_out, B, not_5_out);
  nor nor_1 (nor_1_out, A, not_6_out);
  and and_2 (and_2_out, B, nor_1_out);
  and and_3 (and_3_out, B, not_7_out);
  and and_4 (and_4_out, not_8_out, D);
  nor nor_2 (nor_2_out, and_1_out, and_2_out, and_3_out, and_4_out);
  and and_5 (and_5_out, A, B, D);
  and and_6 (and_6_out, xor_1_out, nor_2_out);
  nor nor_3 (nor_3_out, not_3_out, and_6_out, and_5_out);
  and and_7 (out_5, or_1_out, nor_3_out);
endmodule
