// Logisim project teste.circ as structural Verilog: 9 circuits, main circuit main
module main (
);

  wire clock_1_out, j_k_ff_1_q, j_k_ff_2_q, j_k_ff_3_q, j_k_ff_3_qn, n7seg_1_a_2, n7seg_1_b_2, n7seg_1_c_2,
       n7seg_1_d_2, n7seg_1_e, n7seg_1_f, n7seg_1_g, not_1_out, or_1_out;

  Clock clock_1 (.out(clock_1_out));
  not not_1 (not_1_out, clock_1_out);
  J_K_Flip_Flop j_k_ff_1 (
    .J(j_k_ff_3_qn), .clk(not_1_out), .K(j_k_ff_3_qn), .Q(j_k_ff_1_q), .en(1'b1));  // open: Qn, preset, reset
  J_K_Flip_Flop j_k_ff_2 (
    .J(or_1_out), .clk(not_1_out), .K(or_1_out), .Q(j_k_ff_2_q), .en(1'b1));  // open: Qn, preset, reset
  or or_1 (or_1_out, j_k_ff_3_qn, j_k_ff_1_q);
  _7SEG u_7seg_1 (
    .C(j_k_ff_3_q), .B(j_k_ff_2_q), .A(j_k_ff_1_q), .G(n7seg_1_g), .F(n7seg_1_f), .A_2(n7seg_1_a_2),
    .B_2(n7seg_1_b_2), .C_2(n7seg_1_c_2), .D_2(n7seg_1_d_2), .E(n7seg_1_e));  // open: D
  _7_Segment_Display u_7_segment_display_1 (
    .g(n7seg_1_g), .f(n7seg_1_f), .a(n7seg_1_a_2), .b(n7seg_1_b_2), .e(n7seg_1_e), .d(n7seg_1_d_2),
    .c(n7seg_1_c_2));  // open: dp
  J_K_Flip_Flop j_k_ff_3 (
    .J(1'b1), .clk(not_1_out), .K(1'b1), .Q(j_k_ff_3_q), .Qn(j_k_ff_3_qn), .en(1'b1));  // open: preset, reset

  // Notes on the sheet:
  //   jk0
  //   jk1
  //   jk2
endmodule

module G (
  input  A,
  input  B,
  input  C,
  input  D,
  output out_5
);

  wire and_1_out, and_2_out, and_3_out, not_1_out, not_2_out, not_3_out;

  and and_1 (and_1_out, B, not_1_out);
  not not_1 (not_1_out, C);
  not not_2 (not_2_out, B);
  and and_2 (and_2_out, not_2_out, C);
  and and_3 (and_3_out, C, not_3_out);
  not not_3 (not_3_out, D);
  or or_1 (out_5, A, and_1_out, and_2_out, and_3_out);
endmodule

module F (
  input  A,
  input  B,
  input  C,
  input  D,
  output out_5
);

  wire and_1_out, and_2_out, and_3_out, not_1_out, not_2_out, not_3_out, not_4_out;

  not not_1 (not_1_out, C);
  and and_1 (and_1_out, not_1_out, not_2_out);
  not not_2 (not_2_out, D);
  and and_2 (and_2_out, B, not_3_out);
  not not_3 (not_3_out, C);
  and and_3 (and_3_out, B, not_4_out);
  not not_4 (not_4_out, D);
  or or_1 (out_5, A, and_1_out, and_2_out, and_3_out);
endmodule

module E (
  input  B,
  input  C,
  input  D,
  output out_4
);

  wire and_1_out, and_2_out, not_1_out, not_2_out, not_3_out;

  not not_1 (not_1_out, B);
  and and_1 (and_1_out, not_1_out, not_2_out);
  not not_2 (not_2_out, D);
  and and_2 (and_2_out, C, not_3_out);
  not not_3 (not_3_out, D);
  or or_1 (out_4, and_1_out, and_2_out);
endmodule

module D (
  input  A,
  input  B,
  input  C,
  input  D,
  output out_5
);

  wire and_1_out, and_2_out, and_3_out, and_4_out, not_1_out, not_2_out, not_3_out, not_4_out, not_5_out;

  not not_1 (not_1_out, B);
  not not_2 (not_2_out, D);
  not not_3 (not_3_out, B);
  not not_4 (not_4_out, D);
  not not_5 (not_5_out, C);
  and and_1 (and_1_out, not_1_out, not_2_out);
  and and_2 (and_2_out, not_3_out, C);
  and and_3 (and_3_out, C, not_4_out);
  and and_4 (and_4_out, B, not_5_out, D);
  or or_1 (out_5, A, and_1_out, and_2_out, and_3_out, and_4_out);
endmodule

module C (
  input  B,
  input  C,
  input  D,
  output out_4
);

  wire not_1_out;

  not not_1 (not_1_out, C);
  or or_1 (out_4, B, not_1_out, D);
endmodule

module B (
  input  B,
  input  C,
  input  D,
  output out_4
);

  wire and_1_out, and_2_out, not_1_out, not_2_out, not_3_out;

  not not_1 (not_1_out, B);
  and and_1 (and_1_out, C, D);
  not not_2 (not_2_out, C);
  and and_2 (and_2_out, not_2_out, not_3_out);
  not not_3 (not_3_out, D);
  or or_1 (out_4, not_1_out, and_1_out, and_2_out);
endmodule

module A (
  input  A,
  input  B,
  input  C,
  input  D,
  output out_5
);

  wire and_1_out, and_2_out, not_1_out, not_2_out;

  not not_1 (not_1_out, B);
  not not_2 (not_2_out, D);
  and and_1 (and_1_out, B, D);
  and and_2 (and_2_out, not_1_out, not_2_out);
  or or_1 (out_5, A, C, and_1_out, and_2_out);
endmodule

module _7SEG (
  input  D,
  input  C,
  input  B,
  input  A,
  output G,
  output F,
  output A_2,
  output B_2,
  output C_2,
  output D_2,
  output E
);

  G g_1 (.out_5(G), .A(D), .B(C), .C(B), .D(A));
  F f_1 (.out_5(F), .A(D), .B(C), .C(B), .D(A));
  A a_1 (.out_5(A_2), .A(D), .B(C), .C(B), .D(A));
  B b_1 (.out_4(B_2), .B(C), .C(B), .D(A));
  C c_1 (.out_4(C_2), .B(C), .C(B), .D(A));
  D d_1 (.out_5(D_2), .A(D), .B(C), .C(B), .D(A));
  E e_1 (.out_4(E), .B(C), .C(B), .D(A));
endmodule
